# Fritzing sketch sampleForTest (saved by Fritzing 0.9.3b)
breadboards: 1

parts:
  Componente1 = Arduino GSM Shield
  U1 = ATTINY13 [package=dip]
  C1 = Capacitor [package=cap-pth-small2]
  R1 = Resistor [tolerance=±5% resistance=220 package="0603 [SMD]"]

nets:
  N1: Componente1.N/C_D0, R1.Pin_1
  N2: Componente1.N/C_D1, U1.PB3(ADC3)
  N3: U1.GND, C1.1
  N4: U1.PB0(MOSI), R1.Pin_0
  N5: U1.VCC, C1.2

notes:
  AttinyISP module
  gnd,sck,miso,mosi,reset
  cp2102
  rxd, gnd
  La resistenza da 1k posta sul pin 0 non blocca ISP durante upload.

custom parts:
  Capacitor: Capacitor Standard 0603 ceramic capacitor, and 0.1 leaded capacitor.
